// Logisim project alu.circ as structural Verilog: 1 circuit, main circuit alu
module alu (
  input  [31:0] A,
  input  [31:0] B,
  input  [3:0] ALUSel,
  output [31:0] ALUResult
);

  wire comparator_1_lt;
  wire [31:0] add0, and7, mul8, mulh9, mulhu11, multiplier_2_out, multiplier_3_out, or6, sll1, slt2, sra13,
       srl5, sub12, xor4;
  wire [63:0] bit_extender_1_out, bit_extender_2_out, bit_extender_3_out, bit_extender_4_out;

  Comparator #(.width(32)) comparator_1 (.a(A), .b(B), .lt(comparator_1_lt));  // open: gt, eq
  assign bit_extender_1_out = {{32{A[31]}}, A};  // Bit_Extender bit_extender_1
  assign bit_extender_2_out = {{32{B[31]}}, B};  // Bit_Extender bit_extender_2
  assign bit_extender_3_out = {{32{1'b0}}, A};  // Bit_Extender bit_extender_3
  assign bit_extender_4_out = {{32{1'b0}}, B};  // Bit_Extender bit_extender_4
  Adder #(.width(32)) adder_1 (.a(A), .b(B), .out(add0));  // open: cin, cout
  Shifter #(.width(32)) shifter_1 (.in(A), .\dist (B[4:0]), .out(sll1));
  assign slt2 = {{31{1'b0}}, comparator_1_lt};  // Bit_Extender bit_extender_5
  assign xor4 = A ^ B;  // XOR_Gate xor_1, 32 bits wide
  Shifter #(.shift("lr"), .width(32)) shifter_2 (.in(A), .\dist (B[4:0]), .out(srl5));
  assign or6 = A | B;  // OR_Gate or_1, 32 bits wide
  assign and7 = A & B;  // AND_Gate and_1, 32 bits wide
  Multiplier #(.mode("twosComplement"), .width(32)) multiplier_1 (.a(A), .b(B), .out(mul8));  // open: cin, cout
  Multiplier #(.mode("twosComplement"), .width(64)) multiplier_2 (
    .a(bit_extender_1_out), .b(bit_extender_2_out), .out({mulh9, multiplier_2_out}));  // open: cin, cout
  Multiplier #(.width(64)) multiplier_3 (
    .a(bit_extender_3_out), .b(bit_extender_4_out), .out({mulhu11, multiplier_3_out}));  // open: cin, cout
  Subtractor #(.width(32)) subtractor_1 (.a(A), .b(B), .out(sub12));  // open: bin, bout
  Shifter #(.shift("ar"), .width(32)) shifter_3 (.in(A), .\dist (B[4:0]), .out(sra13));
  Multiplexer #(.select(4), .width(32)) multiplexer_1 (
    .in0(add0), .in1(sll1), .in2(slt2), .in4(xor4), .in5(srl5), .in6(or6), .in7(and7), .in8(mul8),
    .in9(mulh9), .in11(mulhu11), .in12(sub12), .in13(sra13), .in15(B), .out(ALUResult), .sel(ALUSel));  // open: in3, in10, in14

  // Other names for the same wires on the sheet: bsel15[31:0] = B

  // Notes on the sheet:
  //   INPUTS to your circuit
  //   DON'T CHANGE THE LOCATIONS OF THE INPUTS AND OUTPUTS!
  //   OUTPUT from your circuit
endmodule
