// Logisim project control-logic.circ as structural Verilog: 1 circuit, main circuit control_logic
module control_logic (
  input  [31:0] Instruction,
  input  BrEq,
  input  BrLt,
  output PCSel,
  output RegWEn,
  output [2:0] ImmSel,
  output BrUn,
  output ASel,
  output BSel,
  output [3:0] ALUSel,
  output MemWEn,
  output [1:0] WBSel
);

  wire and_15_out, and_16_out, and_17_out, and_18_out, and_19_out, and_20_out, and_26_out, comparator_2_eq,
       comparator_3_eq, comparator_4_eq, comparator_5_eq, comparator_6_eq, comparator_7_eq, comparator_8_eq,
       comparator_9_eq, comparator_10_eq, comparator_11_eq, comparator_12_eq, comparator_13_eq,
       comparator_14_eq, comparator_15_eq, comparator_16_eq, comparator_17_eq, comparator_20_eq,
       comparator_21_eq, comparator_22_eq, comparator_23_eq, comparator_24_eq, comparator_25_eq,
       comparator_26_eq, comparator_27_eq, comparator_28_eq, comparator_29_eq, comparator_30_eq,
       comparator_31_eq, comparator_33_eq, comparator_34_eq, comparator_35_eq, comparator_36_eq,
       comparator_37_eq, comparator_38_eq, comparator_39_eq, comparator_40_eq, comparator_41_eq,
       comparator_42_eq, comparator_43_eq, comparator_44_eq, comparator_45_eq, comparator_46_eq,
       comparator_49_eq, comparator_50_eq, isAdd, isAddi, isAnd, isAndi, isAuipc, isBeq, isBge, isBgeu,
       isBlt, isBltu, isBne, isBType, isIStarType, isIType, isJal, isJalr, isLb, isLh, isLui, isLw, isMul,
       isMulh, isMulhu, isOr, isOri, isRType, isSb, isSh, isSll, isSlli, isSlt, isSlti, isSra, isSrai, isSrl,
       isSrli, isSType, isSub, isSw, isXor, isXori, not_1_out, not_2_out, not_3_out, or_1_out, or_2_out;
  wire [5:0] ROMIn;
  wire [15:14] rom_1_data;

  ROM #(.addrWidth(6), .dataWidth(16)) rom_1 (
    .addr(ROMIn), .data({rom_1_data, WBSel, MemWEn, ALUSel, BSel, ASel, BrUn, ImmSel, RegWEn}));
  Priority_Encoder #(.select_enc(6)) priority_encoder_1 (
    .in0(isLb), .in1(isLh), .in2(isLw), .in3(isAddi), .in4(isSlli), .in5(isSlti), .in6(isXori), .in7(isSrli),
    .in8(isSrai), .in9(isOri), .in10(isAndi), .in11(isAdd), .in12(isMul), .in13(isSub), .in14(isSll),
    .in15(isMulh), .in16(isMulhu), .in17(isSlt), .in18(isXor), .in19(isSrl), .in20(isSra), .in21(isOr),
    .in22(isAnd), .in23(isBeq), .in24(isBne), .in25(isBlt), .in26(isBge), .in27(isBltu), .in28(isBgeu),
    .in29(isSb), .in30(isSh), .in31(isSw), .in32(isJal), .in33(isJalr), .in34(isAuipc), .in35(isLui),
    .out(ROMIn));  // open: in36, in37, in38, in39, in40, in41, in42, in43, in44, in45, in46, in47, in48, in49, in50, in51, in52, in53, in54, in55, in56, in57, in58, in59, in60, in61, in62, in63, gs, en_out, en_in
  Comparator #(.width(7)) comparator_1 (.a(Instruction[6:0]), .b(7'b0010011), .eq(isIType));  // open: gt, lt
  Comparator #(.width(3)) comparator_2 (.a(Instruction[14:12]), .b(3'b000), .eq(comparator_2_eq));  // open: gt, lt
  Comparator #(.width(3)) comparator_3 (.a(Instruction[14:12]), .b(3'b001), .eq(comparator_3_eq));  // open: gt, lt
  Comparator #(.width(3)) comparator_4 (.a(Instruction[14:12]), .b(3'b101), .eq(comparator_4_eq));  // open: gt, lt
  Comparator #(.width(7)) comparator_5 (.a(Instruction[31:25]), .b(7'b0100000), .eq(comparator_5_eq));  // open: gt, lt
  Comparator #(.width(3)) comparator_6 (.a(Instruction[14:12]), .b(3'b101), .eq(comparator_6_eq));  // open: gt, lt
  Comparator #(.width(3)) comparator_7 (.a(Instruction[14:12]), .b(3'b111), .eq(comparator_7_eq));  // open: gt, lt
  Comparator #(.width(3)) comparator_8 (.a(Instruction[14:12]), .b(3'b110), .eq(comparator_8_eq));  // open: gt, lt
  Comparator #(.width(3)) comparator_9 (.a(Instruction[14:12]), .b(3'b000), .eq(comparator_9_eq));  // open: gt, lt
  Comparator #(.width(3)) comparator_10 (.a(Instruction[14:12]), .b(3'b001), .eq(comparator_10_eq));  // open: gt, lt
  Comparator #(.width(3)) comparator_11 (.a(Instruction[14:12]), .b(3'b010), .eq(comparator_11_eq));  // open: gt, lt
  Comparator #(.width(3)) comparator_12 (.a(Instruction[14:12]), .b(3'b000), .eq(comparator_12_eq));  // open: gt, lt
  Comparator #(.width(3)) comparator_13 (.a(Instruction[14:12]), .b(3'b001), .eq(comparator_13_eq));  // open: gt, lt
  Comparator #(.width(3)) comparator_14 (.a(Instruction[14:12]), .b(3'b010), .eq(comparator_14_eq));  // open: gt, lt
  Comparator #(.width(3)) comparator_15 (.a(Instruction[14:12]), .b(3'b010), .eq(comparator_15_eq));  // open: gt, lt
  Comparator #(.width(3)) comparator_16 (.a(Instruction[14:12]), .b(3'b100), .eq(comparator_16_eq));  // open: gt, lt
  Comparator #(.width(7)) comparator_17 (.a(Instruction[31:25]), .b({7{1'b0}}), .eq(comparator_17_eq));  // open: gt, lt
  Comparator #(.width(7)) comparator_18 (.a(Instruction[6:0]), .b(7'b0000011), .eq(isIStarType));  // open: gt, lt
  Comparator #(.width(7)) comparator_19 (.a(Instruction[6:0]), .b(7'b0100011), .eq(isSType));  // open: gt, lt
  and and_1 (isAddi, isIType, comparator_2_eq);
  and and_2 (isSlli, isIType, comparator_3_eq);
  and and_3 (isSlti, isIType, comparator_15_eq);
  and and_4 (isXori, isIType, comparator_16_eq);
  and and_5 (isSrli, isIType, comparator_17_eq, comparator_4_eq);
  and and_6 (isSrai, isIType, comparator_5_eq, comparator_6_eq);
  and and_7 (isAndi, isIType, comparator_7_eq);
  and and_8 (isOri, isIType, comparator_8_eq);
  and and_9 (isLb, isIStarType, comparator_9_eq);
  and and_10 (isLh, isIStarType, comparator_10_eq);
  and and_11 (isLw, isIStarType, comparator_11_eq);
  and and_12 (isSb, isSType, comparator_12_eq);
  and and_13 (isSh, isSType, comparator_13_eq);
  and and_14 (isSw, isSType, comparator_14_eq);
  not not_1 (not_1_out, BrEq);
  not not_2 (not_2_out, BrLt);
  not not_3 (not_3_out, BrLt);
  and and_15 (and_15_out, BrEq, isBeq);
  and and_16 (and_16_out, not_1_out, isBne);
  and and_17 (and_17_out, BrLt, isBlt);
  and and_18 (and_18_out, not_2_out, isBge);
  and and_19 (and_19_out, BrLt, isBltu);
  and and_20 (and_20_out, not_3_out, isBgeu);
  or or_1 (or_1_out, and_15_out, and_16_out, and_17_out, and_18_out, and_19_out, and_20_out);
  Comparator #(.width(3)) comparator_20 (.a(Instruction[14:12]), .b(3'b001), .eq(comparator_20_eq));  // open: gt, lt
  Comparator #(.width(3)) comparator_21 (.a(Instruction[14:12]), .b(3'b001), .eq(comparator_21_eq));  // open: gt, lt
  Comparator #(.width(7)) comparator_22 (
    .a(Instruction[31:25]), .b(7'b0000001), .eq(comparator_22_eq));  // open: gt, lt
  Comparator #(.width(3)) comparator_23 (.a(Instruction[14:12]), .b(3'b011), .eq(comparator_23_eq));  // open: gt, lt
  Comparator #(.width(3)) comparator_24 (.a(Instruction[14:12]), .b(3'b010), .eq(comparator_24_eq));  // open: gt, lt
  Comparator #(.width(3)) comparator_25 (.a(Instruction[14:12]), .b(3'b100), .eq(comparator_25_eq));  // open: gt, lt
  Comparator #(.width(7)) comparator_26 (.a(Instruction[31:25]), .b({7{1'b0}}), .eq(comparator_26_eq));  // open: gt, lt
  Comparator #(.width(3)) comparator_27 (.a(Instruction[14:12]), .b(3'b101), .eq(comparator_27_eq));  // open: gt, lt
  Comparator #(.width(7)) comparator_28 (
    .a(Instruction[31:25]), .b(7'b0100000), .eq(comparator_28_eq));  // open: gt, lt
  Comparator #(.width(3)) comparator_29 (.a(Instruction[14:12]), .b(3'b101), .eq(comparator_29_eq));  // open: gt, lt
  Comparator #(.width(3)) comparator_30 (.a(Instruction[14:12]), .b(3'b110), .eq(comparator_30_eq));  // open: gt, lt
  Comparator #(.width(3)) comparator_31 (.a(Instruction[14:12]), .b(3'b111), .eq(comparator_31_eq));  // open: gt, lt
  Comparator #(.width(7)) comparator_32 (.a(Instruction[6:0]), .b(7'b0110011), .eq(isRType));  // open: gt, lt
  Comparator #(.width(7)) comparator_33 (.a(Instruction[31:25]), .b({7{1'b0}}), .eq(comparator_33_eq));  // open: gt, lt
  Comparator #(.width(3)) comparator_34 (.a(Instruction[14:12]), .b(3'b000), .eq(comparator_34_eq));  // open: gt, lt
  Comparator #(.width(7)) comparator_35 (
    .a(Instruction[31:25]), .b(7'b0000001), .eq(comparator_35_eq));  // open: gt, lt
  Comparator #(.width(3)) comparator_36 (.a(Instruction[14:12]), .b(3'b000), .eq(comparator_36_eq));  // open: gt, lt
  Comparator #(.width(7)) comparator_37 (
    .a(Instruction[31:25]), .b(7'b0100000), .eq(comparator_37_eq));  // open: gt, lt
  Comparator #(.width(3)) comparator_38 (.a(Instruction[14:12]), .b(3'b000), .eq(comparator_38_eq));  // open: gt, lt
  Comparator #(.width(7)) comparator_39 (.a(Instruction[31:25]), .b({7{1'b0}}), .eq(comparator_39_eq));  // open: gt, lt
  Comparator #(.width(7)) comparator_40 (
    .a(Instruction[31:25]), .b(7'b0000001), .eq(comparator_40_eq));  // open: gt, lt
  and and_21 (isXor, isRType, comparator_25_eq);
  and and_22 (isSrl, isRType, comparator_26_eq, comparator_27_eq);
  and and_23 (isSra, isRType, comparator_28_eq, comparator_29_eq);
  and and_24 (isOr, isRType, comparator_30_eq);
  and and_25 (isAnd, isRType, comparator_31_eq);
  or or_2 (or_2_out, isJal, isJalr);
  and and_26 (and_26_out, isBType, or_1_out);
  and and_27 (isAdd, isRType, comparator_33_eq, comparator_34_eq);
  and and_28 (isMul, isRType, comparator_35_eq, comparator_36_eq);
  and and_29 (isSub, isRType, comparator_37_eq, comparator_38_eq);
  and and_30 (isSll, isRType, comparator_39_eq, comparator_20_eq);
  and and_31 (isMulh, isRType, comparator_40_eq, comparator_21_eq);
  and and_32 (isMulhu, isRType, comparator_22_eq, comparator_23_eq);
  and and_33 (isSlt, isRType, comparator_24_eq);
  or or_3 (PCSel, or_2_out, and_26_out);
  Comparator #(.width(3)) comparator_41 (.a(Instruction[14:12]), .b(3'b000), .eq(comparator_41_eq));  // open: gt, lt
  Comparator #(.width(3)) comparator_42 (.a(Instruction[14:12]), .b(3'b001), .eq(comparator_42_eq));  // open: gt, lt
  Comparator #(.width(3)) comparator_43 (.a(Instruction[14:12]), .b(3'b100), .eq(comparator_43_eq));  // open: gt, lt
  Comparator #(.width(3)) comparator_44 (.a(Instruction[14:12]), .b(3'b101), .eq(comparator_44_eq));  // open: gt, lt
  Comparator #(.width(3)) comparator_45 (.a(Instruction[14:12]), .b(3'b110), .eq(comparator_45_eq));  // open: gt, lt
  Comparator #(.width(3)) comparator_46 (.a(Instruction[14:12]), .b(3'b111), .eq(comparator_46_eq));  // open: gt, lt
  Comparator #(.width(7)) comparator_47 (.a(Instruction[6:0]), .b(7'b1100011), .eq(isBType));  // open: gt, lt
  and and_34 (isBeq, isBType, comparator_41_eq);
  and and_35 (isBne, isBType, comparator_42_eq);
  and and_36 (isBlt, isBType, comparator_43_eq);
  and and_37 (isBge, isBType, comparator_44_eq);
  and and_38 (isBltu, isBType, comparator_45_eq);
  and and_39 (isBgeu, isBType, comparator_46_eq);
  Comparator #(.width(7)) comparator_48 (.a(Instruction[6:0]), .b(7'b1101111), .eq(isJal));  // open: gt, lt
  Comparator #(.width(7)) comparator_49 (.a(Instruction[6:0]), .b(7'b1100111), .eq(comparator_49_eq));  // open: gt, lt
  Comparator #(.width(3)) comparator_50 (.a(Instruction[14:12]), .b(3'b000), .eq(comparator_50_eq));  // open: gt, lt
  Comparator #(.width(7)) comparator_51 (.a(Instruction[6:0]), .b(7'b0010111), .eq(isAuipc));  // open: gt, lt
  Comparator #(.width(7)) comparator_52 (.a(Instruction[6:0]), .b(7'b0110111), .eq(isLui));  // open: gt, lt
  and and_40 (isJalr, comparator_49_eq, comparator_50_eq);

  // Other names for the same wires on the sheet: opcode[6:0] = Instruction[6:0]; rd[4:0] = Instruction[11:7];
  //   funct3[2:0] = Instruction[14:12]; rs1[4:0] = Instruction[19:15]; funct7[6:0] = Instruction[31:25]

  // Notes on the sheet:
  //   INPUTS to your circuit
  //   Connect ROM Input here ->
  //   contents of rom_1 (hex, n*v repeats v):
  //   41 41 41 1041 10c1 1141 1241 12c1 16c1 1341 13c1 1001 1401 1601 1081 1481 1581 1101 1201 1281 1681
  //   1301 1381 4*64 74 74 442 442 442 2069 2041 1047 17c7
  //   ROM FOR CONTROL LOGIC
  //   DON'T CHANGE THE LOCATIONS OF THE INPUTS AND OUTPUTS!
  //   This is only if you choose to do the ROM option
  //   CONNECT
  //   WIRE
  //   TO
  //   USE
  //   ROM
  //   OUTPUT from your circuit
  //   I-Type
  //   Reminder: If using ROM, use combinational logic for PCSel
  //   R-Type
  //   B-Type
  //   Jump
  //   U-Type
endmodule
